# Fritzing sketch Auxillary Board (saved by Fritzing 0.9.3b)
circuit board: 6cm x 6cm
perfboards: 1

parts:
  Arduino_Nano = Arduino Nano (Rev3.0)
  Steer = male pin header, 3 pins [form="♂ (male)"]
  Encoder_Signal = male pin header, 4 pins [form="♂ (male)"]
  Drive_Signal = male pin header, 3 pins [form="♂ (male)"]
  Drive_GND = male pin header, 1 pin [form="♂ (male)"]
  Headlights_(Low_Beam) = male pin header, 2 pins [form="♂ (male)"]
  MPU9250 = female pin header, 10 pins [form="♀ (female)"]
  LED_GND = male pin header, 4 pins [form="♂ (male)"]
  Switch = Screw terminal - 2 pins [package=THT]
  Drive_Power = Screw terminal - 2 pins [package=THT]
  Jetson_Nano_Power = Screw terminal - 2 pins [package=THT]
  Reverse_Indicators = male pin header, 2 pins [form="♂ (male)"]
  Right_Indicators = male pin header, 2 pins [form="♂ (male)"]
  Left_Indicators = male pin header, 2 pins [form="♂ (male)"]
  Headlights_(High_Beam) = male pin header, 2 pins [form="♂ (male)"]
  Taillights = male pin header, 2 pins [form="♂ (male)"]
  Encoder_Power = male pin header, 4 pins [form="♂ (male)"]

nets:
  N1: Arduino_Nano.GND, Steer.pin3, Drive_GND.pin1, MPU9250.pin2, LED_GND.pin1, LED_GND.pin2, LED_GND.pin3, LED_GND.pin4, Encoder_Power.pin3, Encoder_Power.pin4
  N2: Arduino_Nano.D2, Encoder_Signal.pin1
  N3: Arduino_Nano.D3, Encoder_Signal.pin2
  N4: Arduino_Nano.D4, Encoder_Signal.pin3
  N5: Arduino_Nano.D5, Encoder_Signal.pin4
  N6: Arduino_Nano.D6, Drive_Signal.pin1
  N7: Arduino_Nano.D7, Drive_Signal.pin2
  N8: Arduino_Nano.D8, Drive_Signal.pin3
  N9: Arduino_Nano.D9, Steer.pin1
  N10: Arduino_Nano.D10, Taillights.pin1, Taillights.pin2
  N11: Arduino_Nano.D11/MOSI, Headlights_(Low_Beam).pin1, Headlights_(Low_Beam).pin2
  N12: Arduino_Nano.D12/MISO, Headlights_(High_Beam).pin1, Headlights_(High_Beam).pin2
  N13: Arduino_Nano.VIN, Steer.pin2, Switch.pin2, Drive_Power.pin2, Jetson_Nano_Power.pin2, Encoder_Power.pin1, Encoder_Power.pin2
  N14: Arduino_Nano.5V, MPU9250.pin1
  N15: Arduino_Nano.A5, MPU9250.pin3
  N16: Arduino_Nano.A4, MPU9250.pin4
  N17: Arduino_Nano.A1, Right_Indicators.pin1, Right_Indicators.pin2
  N18: Arduino_Nano.A0, Left_Indicators.pin1, Left_Indicators.pin2
  N19: Arduino_Nano.D13/SCK, Reverse_Indicators.pin1, Reverse_Indicators.pin2
  N20: Switch.pin1, Drive_Power.pin1, Jetson_Nano_Power.pin1
