# Fritzing sketch Auxiliary Board (saved by Fritzing 0.9.3b)
circuit board: 12cm x 8cm
breadboards: 1

parts:
  Steer_Servo_RR = male pin header, 3 pins [form="♂ (male)"]
  Steer_Servo_RL = male pin header, 3 pins [form="♂ (male)"]
  Motor_Driver_Rear = Motor Driver 1A Dual TB6612FNG
  Motor_Driver_Front = Motor Driver 1A Dual TB6612FNG
  Steer_Servo_FL = male pin header, 3 pins [form="♂ (male)"]
  MPU9250 = female pin header, 10 pins [form="♀ (female)"]
  LED_GND = male pin header, 4 pins [form="♂ (male)"]
  RL_Encoder_1 = male pin header, 1 pin [form="♂ (male)"]
  RL_Encoder_2 = male pin header, 1 pin [form="♂ (male)"]
  RR_Encoder_1 = male pin header, 1 pin [form="♂ (male)"]
  RR_Encoder_2 = male pin header, 1 pin [form="♂ (male)"]
  FL_Encoder_1 = male pin header, 1 pin [form="♂ (male)"]
  FL_Encoder_2 = male pin header, 1 pin [form="♂ (male)"]
  FR_Encoder_2 = male pin header, 1 pin [form="♂ (male)"]
  FR_Encoder_1 = male pin header, 1 pin [form="♂ (male)"]
  Taillights = male pin header, 2 pins [form="♂ (male)"]
  Headlights_(High_Beam) = male pin header, 2 pins [form="♂ (male)"]
  Headlights_(Low_Beam) = male pin header, 2 pins [form="♂ (male)"]
  Reverse_Indicators = male pin header, 2 pins [form="♂ (male)"]
  Left_Indicators = male pin header, 2 pins [form="♂ (male)"]
  Right_Indicators = male pin header, 2 pins [form="♂ (male)"]
  Steer_Servo_FR = male pin header, 3 pins [form="♂ (male)"]
  Buzzer = Buzzer 12mm [package=buzzer-12mm-ns]
  Microphone_Power = male pin header, 2 pins [form="♂ (male)"]
  Microphone = male pin header, 2 pins [form="♂ (male)"]
  Encoder_Power = male pin header, 4 pins [form="♂ (male)"]
  Encoder_GND = male pin header, 4 pins [form="♂ (male)"]
  Drive_Motor_FL = screw terminal, 2 pins
  Drive_Motor_FR = screw terminal, 2 pins
  Drive_Motor_RL = screw terminal, 2 pins
  Drive_Motor_RR = screw terminal, 2 pins
  Auxiliary_Power = screw terminal, 2 pins
  Source_Power = screw terminal, 2 pins
  MCU = Arduino Mega 2560 (Rev3)

nets:
  GND: Steer_Servo_RR.pin1, Steer_Servo_RL.pin1, Motor_Driver_Rear.GND, Motor_Driver_Front.GND, Steer_Servo_FL.pin1, MPU9250.pin2, LED_GND.pin1, LED_GND.pin2, LED_GND.pin3, LED_GND.pin4, Steer_Servo_FR.pin1, Buzzer.2, Microphone_Power.pin1, Encoder_GND.pin1, Encoder_GND.pin2, Encoder_GND.pin3, Encoder_GND.pin4, Auxiliary_Power.pin1, Source_Power.pin1, MCU.GND
  VCC: Steer_Servo_RR.pin2, Steer_Servo_RL.pin2, Motor_Driver_Rear.VCC, Motor_Driver_Rear.VM, Motor_Driver_Front.VCC, Motor_Driver_Front.VM, Steer_Servo_FL.pin2, MPU9250.pin1, Steer_Servo_FR.pin2, Microphone_Power.pin2, Encoder_Power.pin1, Encoder_Power.pin2, Encoder_Power.pin3, Encoder_Power.pin4, Auxiliary_Power.pin2, Source_Power.pin2, MCU.VIN
  N1: Steer_Servo_RR.pin3, MCU.D5_PWM
  N2: Steer_Servo_RL.pin3, MCU.D4_PWM
  N3: Motor_Driver_Rear.B01, Drive_Motor_RL.pin1
  N4: Motor_Driver_Rear.B02, Drive_Motor_RL.pin2
  N5: Motor_Driver_Rear.A02, Drive_Motor_RR.pin1
  N6: Motor_Driver_Rear.A01, Drive_Motor_RR.pin2
  N7: Motor_Driver_Rear.PWMA, MCU.D8_PWM
  N8: Motor_Driver_Rear.AIN2, MCU.A6
  N9: Motor_Driver_Rear.AIN1, MCU.A5
  N10: Motor_Driver_Rear.STBY, MCU.A4
  N11: Motor_Driver_Rear.BIN1, MCU.A3
  N12: Motor_Driver_Rear.BIN2, MCU.A2
  N13: Motor_Driver_Rear.PWMB, MCU.D9_PWM
  N14: Motor_Driver_Front.B01, Drive_Motor_FL.pin1
  N15: Motor_Driver_Front.B02, Drive_Motor_FL.pin2
  N16: Motor_Driver_Front.A02, Drive_Motor_FR.pin1
  N17: Motor_Driver_Front.A01, Drive_Motor_FR.pin2
  N18: Motor_Driver_Front.PWMA, MCU.D10_PWM
  N19: Motor_Driver_Front.AIN2, MCU.A11
  N20: Motor_Driver_Front.AIN1, MCU.A10
  N21: Motor_Driver_Front.STBY, MCU.A9
  N22: Motor_Driver_Front.BIN1, MCU.A8
  N23: Motor_Driver_Front.BIN2, MCU.A7
  N24: Motor_Driver_Front.PWMB, MCU.D11_PWM
  N25: Steer_Servo_FL.pin3, MCU.D7_PWM
  N26: MPU9250.pin3, MCU.D21/SCL, MCU.SCL
  N27: MPU9250.pin4, MCU.D20/SDA, MCU.SDA
  N28: RL_Encoder_1.pin1, MCU.D18/TX1
  N29: RL_Encoder_2.pin1, MCU.D16_PWM/TX2
  N30: RR_Encoder_1.pin1, MCU.D19/RX1
  N31: RR_Encoder_2.pin1, MCU.D17_PWM/RX2
  N32: FL_Encoder_1.pin1, MCU.D3_PWM
  N33: FL_Encoder_2.pin1, MCU.D14/TX3
  N34: FR_Encoder_2.pin1, MCU.D15/RX3
  N35: FR_Encoder_1.pin1, MCU.D2_PWM
  N36: Taillights.pin1, Taillights.pin2, MCU.D45
  N37: Headlights_(High_Beam).pin1, Headlights_(High_Beam).pin2, MCU.D37
  N38: Headlights_(Low_Beam).pin1, Headlights_(Low_Beam).pin2, MCU.D35
  N39: Reverse_Indicators.pin1, Reverse_Indicators.pin2, MCU.D43
  N40: Left_Indicators.pin1, Left_Indicators.pin2, MCU.D39
  N41: Right_Indicators.pin1, Right_Indicators.pin2, MCU.D41
  N42: Steer_Servo_FR.pin3, MCU.D6_PWM
  N43: Buzzer.1, MCU.D46
  N44: Microphone.pin1, MCU.A0
  N45: Microphone.pin2, MCU.A1

notes:
  E11
  E21
  E12
  E22
  L1
  L2
  L3
  L4
  L5
  S2
  S1
  E31
  E41
  E42
  E32
  S4
  S3
  M1
  M2
  M4
  M3
  D1
  D2
  IMU
  LED GND
  LED
  ENC GND
  AUX PWR
  SRC PWR
  B1
  Q1
  MIC PWR
  L6
  MCU
  ENC PWR
  autodrive-ecosystem.github.io
  AutoDRIVE Ecosystem
  +
  -
  Servos
  Mic
  LEDs
  Encoders
  Buzzer
  Motors
  Power
  +5V
  GND
